# Fritzing sketch DotMatrix_RTCDS3231_Arduino (saved by Fritzing 0.9.3b)
breadboards: 1

parts:
  Part2 = Arduino Uno (Rev3) - ICSP
  ZS-042_RTC2 = ZS-042 RTC Module
  S1 = Pushbutton [package="[THT]"]
  S2 = Pushbutton [package="[THT]"]
  S3 = Pushbutton [package="[THT]"]
  M1 = MAX7219 8x8 single Led Matrix Module
  M2 = MAX7219 8x8 single Led Matrix Module  # not connected
  M3 = MAX7219 8x8 single Led Matrix Module  # not connected
  M4 = MAX7219 8x8 single Led Matrix Module  # not connected

nets:
  GND: Part2.GND, ZS-042_RTC2.GND, S1.Pin_3, S1.Pin_4, S2.Pin_3, S2.Pin_4, S3.Pin_3, S3.Pin_4, M1.I-GND, M1.O-GND
  N1: Part2.D11_PWM/MOSI, M1.I-DIN
  N2: Part2.D13/SCK, M1.I-CLK, M1.O-CLK
  N3: Part2.A4/SDA, ZS-042_RTC2.SDA
  N4: Part2.A5/SCL, ZS-042_RTC2.SCL
  N5: Part2.D3_PWM, M1.I-CS, M1.O-CS
  N6: Part2.D5_PWM, S3.Pin_1, S3.Pin_2
  N7: Part2.D6_PWM, S2.Pin_1, S2.Pin_2
  N8: Part2.D7, S1.Pin_1, S1.Pin_2
  5V: Part2.5V, ZS-042_RTC2.VCC, M1.I-VCC, M1.O-VCC

custom parts:
  MAX7219 8x8 single Led Matrix Module: Description: MAX7219 8x8 LedMatrix single Red Module Dimensions: 32x32mm Documents:
