# Fritzing sketch DotMatrix_RTCDS3231_ESP (saved by Fritzing 0.9.3b)
breadboards: 1

parts:
  ZS-042_RTC2 = ZS-042 RTC Module
  S1 = Pushbutton [package="[THT]"]
  S2 = Pushbutton [package="[THT]"]
  S3 = Pushbutton [package="[THT]"]
  M1 = MAX7219 8x8 single Led Matrix Module
  M2 = MAX7219 8x8 single Led Matrix Module  # not connected
  M3 = MAX7219 8x8 single Led Matrix Module  # not connected
  M4 = MAX7219 8x8 single Led Matrix Module  # not connected
  Mod1 = Amica NodeMCU DevKit 1.0  # not connected

nets:
  N1: ZS-042_RTC2.GND, S1.Pin_3, S1.Pin_4, S2.Pin_3, S2.Pin_4, S3.Pin_3, S3.Pin_4, M1.I-GND, M1.O-GND
  N2: ZS-042_RTC2.VCC, M1.I-VCC, M1.O-VCC
  N3: S1.Pin_1, S1.Pin_2
  N4: S2.Pin_1, S2.Pin_2
  N5: S3.Pin_1, S3.Pin_2

custom parts:
  MAX7219 8x8 single Led Matrix Module: Description: MAX7219 8x8 LedMatrix single Red Module Dimensions: 32x32mm Documents:
  Amica NodeMCU DevKit 1.0: Amica NodeMCU DevKit 1.0 Development Kit based on ESP8266 ESP-12E, integating GPIO, PWM, IIC, 1-Wire and ADC all in one board. Links: NodeMCU information page Github
